# Fritzing sketch smart_flower_pot (saved by Fritzing 1.0.2b)
breadboards: 1

parts:
  OLED_I2C1 = OLED 128x64 I2C Monochrome Display
  M1 = BMP280
  Q1 = PNP-Transistor [package="TO92 [THT]"]
  Dust_Sensor = Grove Dust Sensor
  Relay1 = Relay - 6 pins [package="DIP (Dual Inline) [THT]"]
  R1 = Resistor [tolerance=±5% resistance=220 package="2512 [SMD]"]
  R2 = Resistor [tolerance=±5% resistance=2.2k package="2512 [SMD]"]
  A1 = Particle - Photon2
  WATER_PUMP1 = water pump/motor
  Soil_Moisture_Sensor = SoilWatch 10
  AQ_sensor = MQ-131 breakout

nets:
  N1: OLED_I2C1.SDA, M1.SDA, A1.Pin_17
  N2: OLED_I2C1.SCK, M1.SCL, A1.Pin_18
  VCC: OLED_I2C1.VDD, M1.VIN, Relay1.VCC, A1.Pin_2, Soil_Moisture_Sensor.VCC, AQ_sensor.VCC
  GND: OLED_I2C1.GND, M1.GND, Q1.C, Dust_Sensor.GND, Relay1.GND, R2.Pin_1, A1.Pin_4, A1.Pin_30, WATER_PUMP1.pin_2, Soil_Moisture_Sensor.GND, AQ_sensor.GND
  N3: Q1.E, Relay1.IN, R1.Pin_0
  N4: Q1.B, R2.Pin_0, A1.Pin_14
  N5: Dust_Sensor.VCC, Relay1.ON, R1.Pin_1, A1.Pin_26
  N6: Dust_Sensor.SIG, A1.Pin_24
  N7: Relay1.COM, WATER_PUMP1.pin_1
  N8: A1.Pin_5, Soil_Moisture_Sensor.OUT
  N9: A1.Pin_8, AQ_sensor.AO

custom parts:
  BMP280: Temperature Humidity Barometric presure Sensor, I2C
  Grove Dust Sensor: PPD42 Grove Dust Sensor
  Relay - 6 pins: A DIP stand-in part for whatever IC you want. With 6 pins on a 900mil dual inline package (DIP) footprint.
  Particle - Photon2: The Photon 2 is a microcontroller and Wi-Fi networking developed by particle. Features: 802.11a/b/g/n Wi-Fi, 2.4 GHz and 5 GHz Integrated PCB antenna Integrated U.FL connector for external antenna Integrated RF switch BLE 5 using same antenna as Wi-Fi Realtek RTL8721DM MCU ARM Cortex M33 CPU, 200 MHz 2048 KB (2 MB) user application maximum size 3072 KB (3 MB) of RAM available to user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
  water pump/motor: WATER PUMP BY ARDUBLOCKTR
  SoilWatch 10: SoilWatch 10 - Capacitive soil moisture sensor
  MQ-131 breakout: SKU: 101282
